# Fritzing sketch Breadboard (saved by Fritzing 0.8.3b)
breadboards: 1

parts:
  DHT1 = DHT11 Humitidy and Temperature Sensor
  Part1 = Arduino Uno (Rev3)
  LCD1 = LCD screen
  Part2 = SRF05 Ultrasonic Rangefinder

nets:
  VDD: DHT1.VDD, Part1.5V, LCD1.VDD, LCD1.LED+, Part2.VCC
  N1: DHT1.DATA, Part1.D2
  GND: DHT1.GND, Part1.GND, LCD1.VSS, LCD1.LED-, Part2.GND
  N2: Part1.D8, Part2.Trig
  N3: Part1.D9_PWM, Part2.Echo
  N4: Part1.D10_PWM/SS, LCD1.DB4
  N5: Part1.D11_PWM/MOSI, LCD1.DB5
  N6: Part1.D12/MISO, LCD1.DB6
  N7: Part1.D13/SCK, LCD1.DB7
  N8: Part1.D3_PWM, LCD1.RS
  N9: Part1.D4, LCD1.R/W
  N10: Part1.D5_PWM, LCD1.E
  N11: Part1.D6_PWM, LCD1.V0

custom parts:
  DHT11 Humitidy and Temperature Sensor: DHT11 Humidity and Temperature Sensor
